// Digital circuit CPU.dig as structural Verilog
module CPU (
  input  CLK_RAW,
  input  in_2,
  input  in_14,
  output [31:0] out_3,
  output [31:0] out_4,
  output [31:0] out_5,
  output [31:0] out_6,
  output [31:0] PC,
  output [31:0] ADDR,
  output [31:0] Instr,
  output [7:0] Dout,
  output [4:0] Step,
  output [7:0] Substep,
  output [7:0] Dval,
  output [14:0] out_15,
  output [15:0] out_16,
  output out_17,
  output [31:0] out_18,
  output BUS_CLK,
  output [31:0] out_20,
  output [31:0] out_21,
  output [31:0] out_22
);

  wire ADDR_CLK, ADDR_IN, ADDR_IN_MUX, ADDR_LATCH, ALU_A, ALU_B, ALU_FLAG_LATCH, ALU_N, ALU_OUT,
       alu_shift_step_1_p5, alu_shift_step_1_p6, alu_shift_step_1_p7, BUS_EN, CLK, clock_1_p3, clock_1_p11,
       Const31, d_ff_1_q, demultiplexer_1_out_1, demultiplexer_1_out_2, demultiplexer_1_out_3,
       demultiplexer_1_out_4, IMM_SnP, ImmB, ImmI, ImmJ, ImmS, ImmU, LEN8, LEN32, MEM_IN, MEM_OUT, nADDR_PE,
       nALU_RESET, nCLK, nLASTSTEP, nMEM_OE, nMEM_WE, nOPDONE, not_1_out, nPC_CNT_PE, nREG_IN_EN, nRESET,
       nS_EXT, nSTEPDONE, One_Instruction_out, One_Step_out, One_Substep_out, OP_IN, OP_LATCH, PC_IN,
       PC_IN_LATCH, PC_OUT, PC_OUT_LATCH, PC_OUT_SnP, REG_IN, RESET, ROM_SEL, RS1, Run_out, Stop_out;
  wire [1:0] ALU_A_MUX, REG_IN_MUX;
  wire [2:0] ALU_B_MUX, ALU_OP;
  wire [3:0] opcode_1_p13, opcode_1_p14, RSD;
  wire [7:0] ROM_ADDR, ROM_DATA;
  wire [22:15] MicroCode_d;

  D_FF d_ff_1 (.D(OP_LATCH), .C(CLK), .Q(d_ff_1_q));  // open: nQ
  Reset reset_1 (.out(nRESET));
  Reset #(.invertOutput("false")) reset_2 (.out(RESET));
  Button #(.activeLow("true")) Stop (.out(Stop_out));
  Button #(.activeLow("true")) Run (.out(Run_out));
  Button #(.activeLow("true")) One_Instruction (.out(One_Instruction_out));
  Button #(.activeLow("true")) One_Step (.out(One_Step_out));
  Button #(.activeLow("true")) One_Substep (.out(One_Substep_out));
  PC pc_1 (
    .CLK(CLK), .BUS_CLK(BUS_CLK), .IN(PC_IN), .IN_LATCH(PC_IN_LATCH), .OUT_LATCH(PC_OUT_LATCH),
    .OUT_SnP(PC_OUT_SnP), .CNT_EN(nPC_CNT_PE), .CNT_2(OP_LATCH), .nRESET(nRESET), .OUT(PC_OUT), .PC(PC));
  // OpCode opcode_1: pin names not known; wires that end beside it: BUS_CLK, OP_IN, OP_LATCH, d_ff_1_q, IMM_SnP, nRESET, ImmI, ImmS, ImmB, ImmU, ImmJ, Const31, opcode_1_p13, opcode_1_p14, RSD, out_15[9:5], out_15[12:10], out_15[13], nS_EXT, Instr, out_16
  Clock_driver clock_driver_1 (
    .CLK_RAW(CLK_RAW), .Stop(Stop_out), .Run(Run_out), .One_Instruction(One_Instruction_out),
    .One_Step(One_Step_out), .One_Substep(One_Substep_out), .nSTEPDONE(nSTEPDONE), .nOPDONE(nOPDONE),
    .nRESET(nRESET), .CLK(CLK), .nCLK(nCLK));  // open: nWAKEUP, SLEEP, nWAIT, LED_R, LED_G
  and and_1 (BUS_CLK, CLK, BUS_EN);
  not not_1 (not_1_out, clock_1_p3);
  // Mem mem_1: pin names not known; wires that end beside it: CLK, BUS_CLK, MEM_IN, ADDR_IN, ADDR_LATCH, ADDR_CLK, nADDR_PE, nMEM_OE, nMEM_WE, nRESET, ROM_DATA, nS_EXT, MEM_OUT, ADDR, Dout, Dval, ROM_ADDR, ROM_SEL
  LED led_1 (.in(clock_1_p3));
  LED led_2 (.in(not_1_out));
  Register_bank register_bank_1 (
    .CLK(BUS_CLK), .IN(REG_IN), .nEN_IN(nREG_IN_EN), .SA(opcode_1_p13), .SB(opcode_1_p14), .SD(RSD),
    .RESET(RESET), .A(RS1), .B(MEM_IN));
  // Clock clock_1: pin names not known; wires that end beside it: CLK, nCLK, clock_1_p3, CLK, nCLK, LEN8, LEN32, nLASTSTEP, nRESET, out_15[4:0], clock_1_p11, nSTEPDONE, Substep, nOPDONE, clock_1_p11
  Multiplexer #(.Selector_Bits(3)) multiplexer_1 (
    .sel(ALU_B_MUX), .in_0(MEM_IN), .in_1(ImmI), .in_2(ImmS), .in_3(ImmB), .in_4(ImmU), .in_5(ImmJ),
    .in_6(1'b0), .in_7(1'b0), .out(ALU_B));
  Multiplexer multiplexer_2 (.sel(in_14), .in_0(ALU_OUT), .in_1(1'b0), .out(PC_IN));
  // ALU_shift_step alu_shift_step_1: pin names not known; wires that end beside it: CLK, nCLK, nALU_RESET, nSTEPDONE, alu_shift_step_1_p5, alu_shift_step_1_p6, alu_shift_step_1_p7
  Demultiplexer #(.Selector_Bits(4), .Default(1)) demultiplexer_1 (
    .sel(RSD), .in(nREG_IN_EN), .out_1(demultiplexer_1_out_1), .out_2(demultiplexer_1_out_2),
    .out_3(demultiplexer_1_out_3), .out_4(demultiplexer_1_out_4));  // open: out_0, out_5, out_6, out_7, out_8, out_9, out_10, out_11, out_12, out_13, out_14, out_15
  // ALU alu_1: pin names not known; wires that end beside it: BUS_CLK, ALU_A, ALU_B, ALU_N, nALU_RESET, ALU_FLAG_LATCH, ALU_OP, alu_shift_step_1_p5, alu_shift_step_1_p6, alu_shift_step_1_p7, out_15[14], ALU_OUT, out_17
  Multiplexer #(.Selector_Bits(2)) multiplexer_3 (
    .sel(ALU_A_MUX), .in_0(RS1), .in_1(PC_OUT), .in_2(Const31), .in_3(1'b0), .out(ALU_A));
  Multiplexer multiplexer_4 (.sel(ADDR_IN_MUX), .in_0(ALU_OUT), .in_1(PC_OUT), .out(ADDR_IN));
  DebugShift32 debugshift32_1 (.CLK(BUS_CLK), .D(REG_IN), .nEN(demultiplexer_1_out_1), .Val(out_22));
  DebugShift32 debugshift32_2 (.CLK(BUS_CLK), .D(REG_IN), .nEN(demultiplexer_1_out_2), .Val(out_4));
  DebugShift32 debugshift32_3 (.CLK(BUS_CLK), .D(REG_IN), .nEN(demultiplexer_1_out_3), .Val(out_5));
  DebugShift32 debugshift32_4 (.CLK(BUS_CLK), .D(REG_IN), .nEN(demultiplexer_1_out_4), .Val(out_6));
  D_FF #(.Bits(32)) d_ff_2 (.D(out_22), .C(demultiplexer_1_out_1), .Q(out_3));  // open: nQ
  Multiplexer #(.Selector_Bits(2)) multiplexer_5 (
    .sel(REG_IN_MUX), .in_0(ALU_OUT), .in_1(MEM_OUT), .in_2(1'b0), .in_3(PC_OUT), .out(REG_IN));
  Multiplexer multiplexer_6 (.sel(in_2), .in_0(MEM_OUT), .in_1(1'b0), .out(OP_IN));
  DebugShift32 debugshift32_5 (.CLK(BUS_CLK), .D(ALU_A), .nEN(1'b0), .Val(out_18));
  DebugShift32 debugshift32_6 (.CLK(BUS_CLK), .D(ALU_B), .nEN(1'b0), .Val(out_20));
  DebugShift32 debugshift32_7 (.CLK(BUS_CLK), .D(ALU_OUT), .nEN(1'b0), .Val(out_21));
  ROM #(.AddrBits(15), .isProgramMemory("true"), .Bits(32)) MicroCode (
    .A(out_15), .sel(1'b1),
    .D({ADDR_IN_MUX, REG_IN_MUX, ALU_B_MUX, ALU_A_MUX, IMM_SnP, MicroCode_d[22], OP_LATCH, nMEM_WE, nMEM_OE, nADDR_PE, ADDR_CLK, ADDR_LATCH, MicroCode_d[15], nPC_CNT_PE, PC_OUT_SnP, PC_OUT_LATCH, PC_IN_LATCH, BUS_EN, nREG_IN_EN, nLASTSTEP, LEN32, LEN8, ALU_OP, ALU_FLAG_LATCH, nALU_RESET, ALU_N}));
  ROM #(.AddrBits(8), .Bits(8)) Firmware (.A(ROM_ADDR), .sel(ROM_SEL), .D(ROM_DATA));

  assign Step = out_15[4:0];

  // Other names for the same wires on the sheet: FLAG = out_15[14]; FUNC3[2:0] = out_15[12:10]; Mem_Dout[7:0] = Dout;
  //   Mem_Dval[7:0] = Dval; OP_IN_MUX = in_2; OPCODE[4:0] = out_15[9:5]; PC_IN_MUX = in_14; RS2 = MEM_IN;
  //   SA = out_15[13]

  // Notes on the sheet:
  //   CLK_RAW: Hz: 10000
  //   contents of MicroCode (hex, n*v repeats v):
  //   801c6782,194302,134302,1d4742,174302,1d4742,174302,1d4742,174302,1d4742,3d4302,5dc300,
  //   49c4782,194302,134302,201d4542,201d4542,201d4542,201d4542,201d5002,0,0,0,0,0,0,0,
  //   0,0,0,0,0,801c6782,194302,134302,1d4742,174302,1d4742,174302,1d4742,174302,1d4742,
  //   3d4302,3d4302,3d4302,3d4202,0,0,0,0,0,0,0,0,0,0,0,0,0,0,0,0,0,0,801c6782,194302,134302,
  //   1d4742,174302,1d4742,174302,1d4742,174302,1d4742,3d4302,3d4302,3d4302,3d4202,0,0,
  //   0,0,0,0,0,0,0,0,0,0,0,0,0,0,0,0,801c6782,194302,134302,1d4742,174302,1d4742,174302,
  //   1d4742,174302,1d4742,3d4302,3d4302,3d4302,3d4202,0,0,0,0,0,0,0,0,0,0,0,0,0,0,0,0,
  //   0,0,801c6782,194302,134302,1d4742,174302,1d4742,174302,1d4742,174302,1d4742,3d4302,
  //   5dc300,49d4542,49d4542,49d4542,49d4542,1d5202,0,0,0,0,0,0,0,0,0,0,0,0,0,0,0,801c6782,
  //   194302,134302,1d4742,174302,1d4742,174302,1d4742,174302,1d4742,3d4302,5dc300,119d6542,
  //   119d6542,119d6542,119d6542,1d5202,0,0,0,0,0,0,0,0,0,0,0,0,0,0,0,801c6782,194302,134302,
  //   1d4742,174302,1d4742,174302,1d4742,174302,1d4742,3d4302,3d4302,3d4302,3d4202,0,0,
  //   0,0,0,0,0,0,0,0,0,0,0,0,0,0,0,0,801c6782,194302,134302,1d4742,174302,1d4742,174302,
  //   1d4742,174302,1d4742,3d4302,3d4302,3d4302,3d4202,0,0,0,0,0,0,0,0,0,0,0,0,0,0,0,0,
  //   0,0,801c6782,194302,134302,1d4742,174302,1d4742,174302,1d4742,174302,1d4742,3d4302,
  //   5dc300,89c4782,194302,1a4742,c4302,1c5202,0,0,0,0,0,0,0,0,0,0,0,0,0,0,0,801c6782,
  //   194302,134302,1d4742,174302,1d4742,174302,1d4742,174302,1d4742,3d4302,3d4302,3d4302,
  //   3d4202,0,0,0,0,0,0,0,0,0,0,0,0,0,0,0,0,0,0,801c6782,194302,134302,1d4742,174302,1d4742,
  //   174302,1d4742,174302,1d4742,3d4302,3d4302,3d4302,3d4202,0,0,0,0,0,0,0,0,0,0,0,0,0,
  //   0,0,0,0,0,801c6782,194302,134302,1d4742,174302,1d4742,174302,1d4742,174302,1d4742,
  //   3d4302,3d4302,3d4302,3d4202,0,0,0,0,0,0,0,0,0,0,0,0,0,0,0,0,0,0,801c6782,194302,134302,
  //   1d4742,174302,1d4742,174302,1d4742,174302,1d4742,3d4302,1dc300,1d4542,1d4542,1d4542,
  //   1d4542,1d5202,0,0,0,0,0,0,0,0,0,0,0,0,0,0,0,801c6782,194302,134302,1d4742,174302,
  //   1d4742,174302,1d4742,174302,1d4742,3d4302,5dc300,139d4542,139d4542,139d4542,139d4542,
  //   1d5202,0,0,0,0,0,0,0,0,0,0,0,0,0,0,0,801c6782,194302,134302,1d4742,174302,1d4742,
  //   174302,1d4742,174302,1d4742,3d4302,3d4302,3d4302,3d4202,0,0,0,0,0,0,0,0,0,0,0,0,0,
  //   0,0,0,0,0,801c6782,194302,134302,1d4742,174302,1d4742,174302,1d4742,174302,1d4742,
  //   3d4302,3d4302,3d4302,3d4202,0,0,0,0,0,0,0,0,0,0,0,0,0,0,0,0,0,0,801c6782,194302,134302,
  //   1d4742,174302,1d4742,174302,1d4742,174302,1d4742,3d4302,3d4302,3d4302,3d4202,0,0,
  //   0,0,0,0,0,0,0,0,0,0,0,0,0,0,0,0,801c6782,194302,134302,1d4742,174302,1d4742,174302,
  //   1d4742,174302,1d4742,3d4302,3d4302,3d4302,3d4202,0,0,0,0,0,0,0,0,0,0,0,0,0,0,0,0,
  //   0,0,801c6782,194302,134302,1d4742,174302,1d4742,174302,1d4742,174302,1d4742,3d4302,
  //   3d4302,3d4302,3d4202,0,0,0,0,0,0,0,0,0,0,0,0,0,0,0,0,0,0,801c6782,194302,134302,1d4742,
  //   174302,1d4742,174302,1d4742,174302,1d4742,3d4302,3d4302,3d4302,3d4202,0,0,0,0,0,0,
  //   0,0,0,0,0,0,0,0,0,0,0,0,801c6782,194302,134302,1d4742,174302,1d4742,174302,1d4742,
  //   174302,1d4742,3d4302,3d4302,3d4302,3d4202,0,0,0,0,0,0,0,0,0,0,0,0,0,0,0,0,0,0,801c6782,
  //   194302,134302,1d4742,174302,1d4742,174302,1d4742,174302,1d4742,3d4302,3d4302,3d4302,
  //   3d4202,0,0,0,0,0,0,0,0,0,0,0,0,0,0,0,0,0,0,801c6782,194302,134302,1d4742,174302,1d4742,
  //   174302,1d4742,174302,1d4742,3d4302,3d4302,3d4302,3d4202,0,0,0,0,0,0,0,0,0,0,0,0,0,
  //   0,0,0,0,0,801c6782,194302,134302,1d4742,174302,1d4742,174302,1d4742,174302,1d4742,
  //   3d4302,3d4302,3d4302,3d4202,0,0,0,0,0,0,0,0,0,0,0,0,0,0,0,0,0,0,801c6782,194302,134302,
  //   1d4742,174302,1d4742,174302,1d4742,174302,1d4742,3d4302,3d4302,3d4302,3d4202,0,0,
  //   0,0,0,0,0,0,0,0,0,0,0,0,0,0,0,0,801c6782,194302,134302,1d4742,174302,1d4742,174302,
  //   1d4742,174302,1d4742,3d4302,5dc300,49d4782,1d5300,1d1d2d8a,1d1d120a,0,0,0,0,0,0,0,
  //   0,0,0,0,0,0,0,0,0,801c6782,194302,134302,1d4742,174302,1d4742,174302,1d4742,174302,
  //   1d4742,3d4302,3d4302,3d4302,3d4202,0,0,0,0,0,0,0,0,0,0,0,0,0,0,0,0,0,0,801c6782,194302,
  //   134302,1d4742,174302,1d4742,174302,1d4742,174302,1d4742,3d4302,5dc300,159d6782,1d5300,
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  //   contents of Firmware (hex, n*v repeats v):
  //   93,0,10,0,13,2,f0,1,93,90,10,0,13,2,f2,ff,e3,1c,2,fe,93,1,f0,ff,13,2,f0,1,93,d0,10,
  //   40,13,2,f2,ff,e3,1c,2,fe,6f,f0,df,fd
endmodule
